// Logisim project ex_1.circ as structural Verilog: 5 circuits, main circuit main
module main (
  input  [7:0] in_1,
  input  in_2,
  input  in_3,
  input  in_4,
  input  in_5,
  input  [7:0] in_6,
  input  in_7,
  input  in_8,
  input  in_9,
  input  in_10,
  input  in_11,
  output [7:0] out_12,
  output [3:0] out_13
);

  wire [7:0] reg_a_1_reg_int_out, reg_b_1_reg_int_out;

  Reg_A reg_a_1 (
    .reg_in(in_1), .reg_in_en(in_2), .reg_clk(in_4), .reg_int_out(reg_a_1_reg_int_out));  // open: reg_out_en, reg_out
  Reg_B reg_b_1 (
    .reg_in(in_6), .reg_in_en(in_7), .reg_clk(in_4), .reg_int_out(reg_b_1_reg_int_out));  // open: reg_out_en, reg_out
  ALU alu_1 (
    .alu_in_1(reg_a_1_reg_int_out), .alu_out_en(in_3), .alu_sub(in_5), .alu_in_2(reg_b_1_reg_int_out),
    .alu_out(out_12));  // open: alu_carry_out
  PC pc_1 (.pc_en(in_8), .pc_clk(in_9), .pc_reset(in_10), .pc_out_en(in_11), .pc_out(out_13));
endmodule

module Reg_A (
  input  [7:0] reg_in,
  input  reg_in_en,
  input  reg_clk,
  input  reg_out_en,
  output [7:0] reg_int_out,
  output [7:0] reg_out
);

  wire multiplexer_1_out, multiplexer_2_out, multiplexer_3_out, multiplexer_4_out, multiplexer_5_out,
       multiplexer_6_out, multiplexer_7_out, multiplexer_8_out;

  Multiplexer multiplexer_1 (.in0(reg_int_out[7]), .in1(reg_in[7]), .out(multiplexer_1_out), .sel(reg_in_en));
  D_Flip_Flop d_ff_1 (.D(multiplexer_1_out), .clk(reg_clk), .Q(reg_int_out[7]));  // open: Qn, preset, reset
  assign reg_out[7] = reg_out_en ? reg_int_out[7] : 1'bz;  // Controlled_Buffer controlled_buffer_1
  Multiplexer multiplexer_2 (.in0(reg_int_out[6]), .in1(reg_in[6]), .out(multiplexer_2_out), .sel(reg_in_en));
  D_Flip_Flop d_ff_2 (.D(multiplexer_2_out), .clk(reg_clk), .Q(reg_int_out[6]));  // open: Qn, preset, reset
  assign reg_out[6] = reg_out_en ? reg_int_out[6] : 1'bz;  // Controlled_Buffer controlled_buffer_2
  Multiplexer multiplexer_3 (.in0(reg_int_out[5]), .in1(reg_in[5]), .out(multiplexer_3_out), .sel(reg_in_en));
  D_Flip_Flop d_ff_3 (.D(multiplexer_3_out), .clk(reg_clk), .Q(reg_int_out[5]));  // open: Qn, preset, reset
  assign reg_out[5] = reg_out_en ? reg_int_out[5] : 1'bz;  // Controlled_Buffer controlled_buffer_3
  Multiplexer multiplexer_4 (.in0(reg_int_out[4]), .in1(reg_in[4]), .out(multiplexer_4_out), .sel(reg_in_en));
  D_Flip_Flop d_ff_4 (.D(multiplexer_4_out), .clk(reg_clk), .Q(reg_int_out[4]));  // open: Qn, preset, reset
  assign reg_out[4] = reg_out_en ? reg_int_out[4] : 1'bz;  // Controlled_Buffer controlled_buffer_4
  Multiplexer multiplexer_5 (.in0(reg_int_out[3]), .in1(reg_in[3]), .out(multiplexer_5_out), .sel(reg_in_en));
  D_Flip_Flop d_ff_5 (.D(multiplexer_5_out), .clk(reg_clk), .Q(reg_int_out[3]));  // open: Qn, preset, reset
  assign reg_out[3] = reg_out_en ? reg_int_out[3] : 1'bz;  // Controlled_Buffer controlled_buffer_5
  Multiplexer multiplexer_6 (.in0(reg_int_out[2]), .in1(reg_in[2]), .out(multiplexer_6_out), .sel(reg_in_en));
  D_Flip_Flop d_ff_6 (.D(multiplexer_6_out), .clk(reg_clk), .Q(reg_int_out[2]));  // open: Qn, preset, reset
  assign reg_out[2] = reg_out_en ? reg_int_out[2] : 1'bz;  // Controlled_Buffer controlled_buffer_6
  Multiplexer multiplexer_7 (.in0(reg_int_out[1]), .in1(reg_in[1]), .out(multiplexer_7_out), .sel(reg_in_en));
  D_Flip_Flop d_ff_7 (.D(multiplexer_7_out), .clk(reg_clk), .Q(reg_int_out[1]));  // open: Qn, preset, reset
  assign reg_out[1] = reg_out_en ? reg_int_out[1] : 1'bz;  // Controlled_Buffer controlled_buffer_7
  Multiplexer multiplexer_8 (.in0(reg_int_out[0]), .in1(reg_in[0]), .out(multiplexer_8_out), .sel(reg_in_en));
  D_Flip_Flop d_ff_8 (.D(multiplexer_8_out), .clk(reg_clk), .Q(reg_int_out[0]));  // open: Qn, preset, reset
  assign reg_out[0] = reg_out_en ? reg_int_out[0] : 1'bz;  // Controlled_Buffer controlled_buffer_8
endmodule

module ALU (
  input  [7:0] alu_in_1,
  input  alu_out_en,
  input  alu_sub,
  input  [7:0] alu_in_2,
  output alu_carry_out,
  output [7:0] alu_out
);

  wire adder_2_cout, adder_3_cout, adder_4_cout, adder_5_cout, adder_6_cout, adder_7_cout, adder_8_cout,
       xor_1_out, xor_2_out, xor_3_out, xor_4_out, xor_5_out, xor_6_out, xor_7_out, xor_8_out;
  wire [7:0] adder_8_out;

  xor xor_1 (xor_1_out, alu_in_2[7], alu_sub);
  Adder #(.width(1)) adder_1 (
    .a(alu_in_1[7]), .b(xor_1_out), .out(adder_8_out[7]), .cin(adder_2_cout), .cout(alu_carry_out));
  xor xor_2 (xor_2_out, alu_in_2[6], alu_sub);
  Adder #(.width(1)) adder_2 (
    .a(alu_in_1[6]), .b(xor_2_out), .out(adder_8_out[6]), .cin(adder_3_cout), .cout(adder_2_cout));
  xor xor_3 (xor_3_out, alu_in_2[5], alu_sub);
  Adder #(.width(1)) adder_3 (
    .a(alu_in_1[5]), .b(xor_3_out), .out(adder_8_out[5]), .cin(adder_4_cout), .cout(adder_3_cout));
  xor xor_4 (xor_4_out, alu_in_2[4], alu_sub);
  Adder #(.width(1)) adder_4 (
    .a(alu_in_1[4]), .b(xor_4_out), .out(adder_8_out[4]), .cin(adder_5_cout), .cout(adder_4_cout));
  xor xor_5 (xor_5_out, alu_in_2[3], alu_sub);
  Adder #(.width(1)) adder_5 (
    .a(alu_in_1[3]), .b(xor_5_out), .out(adder_8_out[3]), .cin(adder_6_cout), .cout(adder_5_cout));
  xor xor_6 (xor_6_out, alu_in_2[2], alu_sub);
  Adder #(.width(1)) adder_6 (
    .a(alu_in_1[2]), .b(xor_6_out), .out(adder_8_out[2]), .cin(adder_7_cout), .cout(adder_6_cout));
  Adder #(.width(1)) adder_7 (
    .a(alu_in_1[1]), .b(xor_7_out), .out(adder_8_out[1]), .cin(adder_8_cout), .cout(adder_7_cout));
  xor xor_7 (xor_7_out, alu_in_2[1], alu_sub);
  xor xor_8 (xor_8_out, alu_in_2[0], alu_sub);
  Adder #(.width(1)) adder_8 (.a(alu_in_1[0]), .b(xor_8_out), .out(adder_8_out[0]), .cin(alu_sub), .cout(adder_8_cout));
  assign alu_out = alu_out_en ? adder_8_out : 8'bz;  // Controlled_Buffer controlled_buffer_1
endmodule

module PC (
  input  pc_en,
  input  pc_clk,
  input  pc_reset,
  input  pc_out_en,
  output [3:0] pc_out
);

  wire j_k_ff_1_qn, j_k_ff_2_qn, j_k_ff_3_qn;
  wire [3:0] j_k_ff_1_q;

  J_K_Flip_Flop j_k_ff_1 (
    .J(pc_en), .K(pc_en), .clk(pc_clk), .Q(j_k_ff_1_q[0]), .Qn(j_k_ff_1_qn), .reset(pc_reset));  // open: preset
  J_K_Flip_Flop j_k_ff_2 (
    .J(pc_en), .K(pc_en), .clk(j_k_ff_1_qn), .Q(j_k_ff_1_q[1]), .Qn(j_k_ff_2_qn), .reset(pc_reset));  // open: preset
  J_K_Flip_Flop j_k_ff_3 (
    .J(pc_en), .K(pc_en), .clk(j_k_ff_2_qn), .Q(j_k_ff_1_q[2]), .Qn(j_k_ff_3_qn), .reset(pc_reset));  // open: preset
  J_K_Flip_Flop j_k_ff_4 (
    .J(pc_en), .K(pc_en), .clk(j_k_ff_3_qn), .Q(j_k_ff_1_q[3]), .reset(pc_reset));  // open: Qn, preset
  assign pc_out = pc_out_en ? j_k_ff_1_q : 4'bz;  // Controlled_Buffer controlled_buffer_1
endmodule

module Reg_B (
  input  [7:0] reg_in,
  input  reg_in_en,
  input  reg_clk,
  input  reg_out_en,
  output [7:0] reg_int_out,
  output [7:0] reg_out
);

  wire multiplexer_1_out, multiplexer_2_out, multiplexer_3_out, multiplexer_4_out, multiplexer_5_out,
       multiplexer_6_out, multiplexer_7_out, multiplexer_8_out;

  Multiplexer multiplexer_1 (.in0(reg_int_out[7]), .in1(reg_in[7]), .out(multiplexer_1_out), .sel(reg_in_en));
  D_Flip_Flop d_ff_1 (.D(multiplexer_1_out), .clk(reg_clk), .Q(reg_int_out[7]));  // open: Qn, preset, reset
  assign reg_out[7] = reg_out_en ? reg_int_out[7] : 1'bz;  // Controlled_Buffer controlled_buffer_1
  Multiplexer multiplexer_2 (.in0(reg_int_out[6]), .in1(reg_in[6]), .out(multiplexer_2_out), .sel(reg_in_en));
  D_Flip_Flop d_ff_2 (.D(multiplexer_2_out), .clk(reg_clk), .Q(reg_int_out[6]));  // open: Qn, preset, reset
  assign reg_out[6] = reg_out_en ? reg_int_out[6] : 1'bz;  // Controlled_Buffer controlled_buffer_2
  Multiplexer multiplexer_3 (.in0(reg_int_out[5]), .in1(reg_in[5]), .out(multiplexer_3_out), .sel(reg_in_en));
  D_Flip_Flop d_ff_3 (.D(multiplexer_3_out), .clk(reg_clk), .Q(reg_int_out[5]));  // open: Qn, preset, reset
  assign reg_out[5] = reg_out_en ? reg_int_out[5] : 1'bz;  // Controlled_Buffer controlled_buffer_3
  Multiplexer multiplexer_4 (.in0(reg_int_out[4]), .in1(reg_in[4]), .out(multiplexer_4_out), .sel(reg_in_en));
  D_Flip_Flop d_ff_4 (.D(multiplexer_4_out), .clk(reg_clk), .Q(reg_int_out[4]));  // open: Qn, preset, reset
  assign reg_out[4] = reg_out_en ? reg_int_out[4] : 1'bz;  // Controlled_Buffer controlled_buffer_4
  Multiplexer multiplexer_5 (.in0(reg_int_out[3]), .in1(reg_in[3]), .out(multiplexer_5_out), .sel(reg_in_en));
  D_Flip_Flop d_ff_5 (.D(multiplexer_5_out), .clk(reg_clk), .Q(reg_int_out[3]));  // open: Qn, preset, reset
  assign reg_out[3] = reg_out_en ? reg_int_out[3] : 1'bz;  // Controlled_Buffer controlled_buffer_5
  Multiplexer multiplexer_6 (.in0(reg_int_out[2]), .in1(reg_in[2]), .out(multiplexer_6_out), .sel(reg_in_en));
  D_Flip_Flop d_ff_6 (.D(multiplexer_6_out), .clk(reg_clk), .Q(reg_int_out[2]));  // open: Qn, preset, reset
  assign reg_out[2] = reg_out_en ? reg_int_out[2] : 1'bz;  // Controlled_Buffer controlled_buffer_6
  Multiplexer multiplexer_7 (.in0(reg_int_out[1]), .in1(reg_in[1]), .out(multiplexer_7_out), .sel(reg_in_en));
  D_Flip_Flop d_ff_7 (.D(multiplexer_7_out), .clk(reg_clk), .Q(reg_int_out[1]));  // open: Qn, preset, reset
  assign reg_out[1] = reg_out_en ? reg_int_out[1] : 1'bz;  // Controlled_Buffer controlled_buffer_7
  Multiplexer multiplexer_8 (.in0(reg_int_out[0]), .in1(reg_in[0]), .out(multiplexer_8_out), .sel(reg_in_en));
  D_Flip_Flop d_ff_8 (.D(multiplexer_8_out), .clk(reg_clk), .Q(reg_int_out[0]));  // open: Qn, preset, reset
  assign reg_out[0] = reg_out_en ? reg_int_out[0] : 1'bz;  // Controlled_Buffer controlled_buffer_8
endmodule
